// Logisim project 8-Bit Princeton CPU.circ as structural Verilog: 2 circuits, main circuit main
module main (
);

  wire A_IN, A_OUT, ADDR_HI, ADDR_LO, clock_1_out, clock_2_out, decoder_1_out0, NEW_OP, NO_COUNT, READ_ADDR,
       ROM_OUT;
  wire [1:0] counter_2_q;
  wire [7:0] Boot_ROM_data, controlled_buffer_1_out, IR_q, register_3_q;
  wire [15:0] counter_1_q, multiplexer_1_out, register_2_q;
  wire [15:1] Control_ROM_data;

  Counter #(.max('hffff), .width(16)) counter_1 (
    .count(NO_COUNT), .Q(counter_1_q), .clk(clock_1_out), .clr(1'b0));  // open: load, D, carry
  Clock clock_1 (.out(clock_1_out));
  Multiplexer #(.enable("false"), .width(16)) multiplexer_1 (
    .in0(counter_1_q), .in1(register_2_q), .out(multiplexer_1_out), .sel(READ_ADDR));
  ROM Boot_ROM (.addr(multiplexer_1_out[7:0]), .data(Boot_ROM_data));
  assign controlled_buffer_1_out = ROM_OUT ? Boot_ROM_data : 8'bz;  // Controlled_Buffer controlled_buffer_1
  Register #(.trigger("high")) register_1 (
    .D(controlled_buffer_1_out), .en(ADDR_HI), .Q(register_2_q[15:8]), .clk(1'b1), .clr(1'b0));
  Register #(.trigger("high")) register_2 (
    .D(controlled_buffer_1_out), .en(ADDR_LO), .Q(register_2_q[7:0]), .clk(1'b1), .clr(1'b0));
  Register #(.trigger("high")) IR (.D(controlled_buffer_1_out), .en(decoder_1_out0), .Q(IR_q), .clk(1'b1), .clr(1'b0));
  Counter #(.max('h3), .width(2)) counter_2 (
    .load(NEW_OP), .D(2'b00), .Q(counter_2_q), .clk(clock_2_out), .clr(1'b0));  // open: count, carry
  Clock clock_2 (.out(clock_2_out));
  Decoder #(.enable("false"), .select(2)) decoder_1 (
    .out0(decoder_1_out0), .sel(counter_2_q));  // open: out1, out2, out3
  ROM #(.addrWidth(10), .dataWidth(16)) Control_ROM (
    .addr({counter_2_q, IR_q}),
    .data({Control_ROM_data[15:8], READ_ADDR, Control_ROM_data[6], ADDR_LO, ADDR_HI, A_OUT, A_IN, Control_ROM_data[1], NEW_OP}));
  Register #(.trigger("high")) register_3 (
    .D(controlled_buffer_1_out), .en(A_IN), .Q(register_3_q), .clk(1'b1), .clr(1'b0));
  assign controlled_buffer_1_out = A_OUT ? register_3_q : 8'bz;  // Controlled_Buffer controlled_buffer_2
  not not_1 (ROM_OUT, Control_ROM_data[1]);
  not not_2 (NO_COUNT, Control_ROM_data[6]);

  // Notes on the sheet:
  //   contents of Boot_ROM (hex, n*v repeats v):
  //   1 a9 2 10 20 ff 26*0 fa
  //   contents of Control_ROM (hex, n*v repeats v):
  //   257*0 5 10 255*0 60 255*0 85
  //   END INSTRUCTION
  //   A_IN
  //   A_OUT
endmodule

module _181_ALU (
  input  Cn,
  input  M,
  input  A0,
  input  B0,
  input  A1,
  input  B1,
  input  A0_2,
  input  B0_2,
  input  A0_3,
  input  B0_3,
  input  S0,
  input  S1,
  input  S2,
  input  S3,
  output F0,
  output F1,
  output A_B,
  output F2,
  output F3,
  output G,
  output Cn_4,
  output P
);

  wire and_1_out, and_2_out, and_3_out, and_4_out, and_5_out, and_6_out, and_7_out, and_8_out, and_10_out,
       and_11_out, and_12_out, and_13_out, and_14_out, and_15_out, and_16_out, and_17_out, and_18_out,
       and_19_out, and_20_out, and_21_out, and_22_out, and_23_out, and_24_out, and_25_out, and_26_out,
       and_27_out, and_28_out, and_29_out, nand_1_out, nand_3_out, nor_1_out, nor_2_out, nor_3_out,
       nor_4_out, nor_5_out, nor_6_out, nor_7_out, nor_8_out, nor_9_out, nor_10_out, nor_11_out, not_1_out,
       not_2_out, not_3_out, not_4_out, not_5_out, xor_2_out, xor_4_out, xor_6_out, xor_8_out;

  nand nand_1 (nand_1_out, Cn, not_1_out);
  not not_1 (not_1_out, M);
  xor xor_1 (F0, nand_1_out, xor_2_out);
  and and_1 (and_1_out, B0, S0);
  nor nor_1 (nor_1_out, A0, and_1_out, and_2_out);
  xor xor_2 (xor_2_out, nor_1_out, nor_3_out);
  not not_2 (not_2_out, B0);
  and and_2 (and_2_out, S1, not_2_out);
  and and_3 (and_3_out, not_1_out, nor_1_out);
  nor nor_2 (nor_2_out, and_3_out, and_5_out);
  and and_4 (and_4_out, not_2_out, S2, A0);
  nor nor_3 (nor_3_out, and_4_out, and_6_out);
  and and_5 (and_5_out, not_1_out, nor_3_out, Cn);
  xor xor_3 (F1, nor_2_out, xor_4_out);
  and and_6 (and_6_out, A0, B0, S3);
  xor xor_4 (xor_4_out, nor_4_out, nor_6_out);
  and and_7 (and_7_out, B1, S0);
  nor nor_4 (nor_4_out, A1, and_7_out, and_10_out);
  and and_8 (and_8_out, not_1_out, nor_4_out);
  and and_9 (A_B, F0, F1, F2, F3);
  not not_3 (not_3_out, B1);
  and and_10 (and_10_out, S1, not_3_out);
  and and_11 (and_11_out, not_1_out, nor_1_out, nor_6_out);
  nor nor_5 (nor_5_out, and_8_out, and_11_out, and_13_out);
  and and_12 (and_12_out, not_3_out, S2, A1);
  nor nor_6 (nor_6_out, and_12_out, and_14_out);
  and and_13 (and_13_out, not_1_out, Cn, nor_3_out, nor_6_out);
  xor xor_5 (F2, nor_5_out, xor_6_out);
  and and_14 (and_14_out, A1, B1, S3);
  xor xor_6 (xor_6_out, nor_7_out, nor_9_out);
  and and_15 (and_15_out, B0_2, S0);
  nor nor_7 (nor_7_out, A0_2, and_15_out, and_17_out);
  and and_16 (and_16_out, not_1_out, nor_7_out);
  not not_4 (not_4_out, B0_2);
  and and_17 (and_17_out, S1, not_4_out);
  and and_18 (and_18_out, not_1_out, nor_4_out, nor_9_out);
  nor nor_8 (nor_8_out, and_16_out, and_18_out, and_20_out, and_21_out);
  and and_19 (and_19_out, not_4_out, S2, A0_2);
  nor nor_9 (nor_9_out, and_19_out, and_22_out);
  and and_20 (and_20_out, not_1_out, nor_1_out, nor_6_out, nor_9_out);
  and and_21 (and_21_out, not_1_out, Cn, nor_3_out, nor_6_out, nor_9_out);
  xor xor_7 (F3, nor_8_out, xor_8_out);
  and and_22 (and_22_out, A0_2, B0_2, S3);
  xor xor_8 (xor_8_out, nor_10_out, nor_11_out);
  and and_23 (and_23_out, B0_3, S0);
  nor nor_10 (nor_10_out, A0_3, and_23_out, and_24_out);
  nand nand_2 (G, nor_3_out, nor_6_out, nor_9_out, nor_11_out);
  nand nand_3 (nand_3_out, Cn, nor_3_out, nor_6_out, nor_9_out, nor_11_out);
  not not_5 (not_5_out, B0_3);
  and and_24 (and_24_out, S1, not_5_out);
  nand nand_4 (Cn_4, nand_3_out, P);
  and and_25 (and_25_out, not_5_out, S2, A0_3);
  nor nor_11 (nor_11_out, and_25_out, and_28_out);
  and and_26 (and_26_out, nor_1_out, nor_6_out, nor_9_out, nor_11_out);
  and and_27 (and_27_out, nor_4_out, nor_9_out, nor_11_out);
  and and_28 (and_28_out, A0_3, B0_3, S3);
  and and_29 (and_29_out, nor_7_out, nor_11_out);
  nor nor_12 (P, and_26_out, and_27_out, and_29_out, nor_10_out);
endmodule
